// Logisim project CPU.circ as structural Verilog
module main (
  input  in_1,
  input  [3:0] ADDRESS,
  input  [7:0] in_3,
  input  [7:0] INPUT,
  input  [7:0] in_5,
  input  in_6,
  input  in_7,
  input  in_8,
  input  in_9,
  input  in_10,
  input  in_11,
  input  in_12,
  input  in_13,
  input  in_14,
  input  in_15,
  input  in_16,
  input  in_17,
  input  in_18,
  output [7:0] OUTPUT,
  output [7:0] out_20,
  output out_21
);

  wire adder_1_a_out, adder_1_c_out, adder_2_a_out, adder_2_c_out;

  \new  new_1 (.in_1(in_13), .in_2(in_14), .out_3(out_21));
  _8_bit_RAM__16_word u_8_bit_ram_16_word_1 (
    .Select_3(ADDRESS[0]), .Select_2(ADDRESS[1]), .Select_1(ADDRESS[2]), .Select_0(ADDRESS[3]),
    .In_7(INPUT[0]), .In_6(INPUT[1]), .In_5(INPUT[2]), .In_4(INPUT[3]), .In_3(INPUT[4]), .In_2(INPUT[5]),
    .In_1(INPUT[6]), .In_0(INPUT[7]), .Reset(in_1), .Set(in_11), .Get(in_12), .Out_7(OUTPUT[0]),
    .Out_6(OUTPUT[1]), .Out_5(OUTPUT[2]), .Out_4(OUTPUT[3]), .Out_3(OUTPUT[4]), .Out_2(OUTPUT[5]),
    .Out_1(OUTPUT[6]), .Out_0(OUTPUT[7]));
  adder adder_1 (._1(in_15), ._2(in_17), .C_in(adder_2_c_out), .A_out(adder_1_a_out), .C_out(adder_1_c_out));
  adder adder_2 (._1(in_16), ._2(in_18), .C_in(1'b0), .A_out(adder_2_a_out), .C_out(adder_2_c_out));
  _8_bit_ram_4_word_x u_8_bit_ram_4_word_x_1 ();  // open: Address, In, Reset, Set, Get, Out
  RAM #(.bus("separate")) ram_1 (
    .addr(in_3), .din(in_5), .data(out_20), .str(in_8), .sel(in_6), .clk(in_9), .ld(in_7), .clr(in_10));
endmodule

module adder (
  input  _1,
  input  _2,
  input  C_in,
  output A_out,
  output C_out
);

  wire and_1_out, and_2_out, buffer_1_out, or_1_out, xor_1_out, xor_2_out;

  buf buffer_1 (buffer_1_out, C_in);
  and and_1 (and_1_out, _2, _1);
  xor xor_1 (xor_1_out, _1, _2);
  xor xor_2 (xor_2_out, xor_1_out, buffer_1_out);
  or or_1 (or_1_out, and_1_out, and_2_out);
  and and_2 (and_2_out, xor_1_out, buffer_1_out);
  buf buffer_2 (C_out, or_1_out);
  buf buffer_3 (A_out, xor_2_out);

  // Notes on the sheet:
  //   Result
endmodule

module _4_Bit_Adder (
  input  B_3,
  input  B_2,
  input  B_1,
  input  B_0,
  input  A_3,
  input  A_2,
  input  A_1,
  input  A_0,
  input  C_In,
  output Out_3,
  output Out_2,
  output Out_1,
  output Out_0,
  output Out_C
);

  wire adder_1_c_out, adder_2_c_out, adder_3_c_out;

  adder adder_1 (._1(B_0), ._2(A_0), .C_in(C_In), .A_out(Out_0), .C_out(adder_1_c_out));
  adder adder_2 (._1(B_2), ._2(A_2), .C_in(adder_3_c_out), .A_out(Out_2), .C_out(adder_2_c_out));
  adder adder_3 (._1(B_1), ._2(A_1), .C_in(adder_1_c_out), .A_out(Out_1), .C_out(adder_3_c_out));
  adder adder_4 (._1(B_3), ._2(A_3), .C_in(adder_2_c_out), .A_out(Out_3), .C_out(Out_C));
endmodule

module _8_Bit_Adder_OLD (
  input  B_7,
  input  B_6,
  input  B_5,
  input  B_4,
  input  B_3,
  input  B_2,
  input  B_1,
  input  B_0,
  input  A_7,
  input  A_6,
  input  A_5,
  input  A_4,
  input  A_3,
  input  A_2,
  input  A_1,
  input  A_0,
  output Out_7,
  output Out_6,
  output Out_5,
  output Out_4,
  output Out_3,
  output Out_2,
  output Out_1,
  output Out_0
);

  wire n4_bit_adder_2_out_c;

  _4_Bit_Adder u_4_bit_adder_1 (
    .B_3(B_7), .B_2(B_6), .B_1(B_5), .B_0(B_4), .A_3(A_7), .A_2(A_6), .A_1(A_5), .A_0(A_4),
    .C_In(n4_bit_adder_2_out_c), .Out_3(Out_7), .Out_2(Out_6), .Out_1(Out_5), .Out_0(Out_4));  // open: Out_C
  _4_Bit_Adder u_4_bit_adder_2 (
    .B_3(B_3), .B_2(B_2), .B_1(B_1), .B_0(B_0), .A_3(A_3), .A_2(A_2), .A_1(A_1), .A_0(A_0), .C_In(1'b0),
    .Out_3(Out_3), .Out_2(Out_2), .Out_1(Out_1), .Out_0(Out_0), .Out_C(n4_bit_adder_2_out_c));
endmodule

module _8_Bit_Adder_Test (
  input  in_1,
  input  in_2,
  input  in_3,
  input  in_4,
  input  in_5,
  input  in_6,
  input  in_7,
  input  in_8,
  input  in_9,
  input  in_10,
  input  in_11,
  input  in_12,
  input  in_13,
  input  in_14,
  input  in_15,
  input  in_16
);

  wire n8_bit_adder_old_1_out_0, n8_bit_adder_old_1_out_1, n8_bit_adder_old_1_out_2,
       n8_bit_adder_old_1_out_3, n8_bit_adder_old_1_out_4, n8_bit_adder_old_1_out_5,
       n8_bit_adder_old_1_out_6, n8_bit_adder_old_1_out_7;

  _8_Bit_Adder_OLD u_8_bit_adder_old_1 (
    .B_7(in_1), .B_6(in_2), .B_5(in_3), .B_4(in_4), .B_3(in_5), .B_2(in_6), .B_1(in_7), .B_0(in_8),
    .A_7(in_9), .A_6(in_10), .A_5(in_11), .A_4(in_12), .A_3(in_13), .A_2(in_14), .A_1(in_15), .A_0(in_16),
    .Out_7(n8_bit_adder_old_1_out_7), .Out_6(n8_bit_adder_old_1_out_6), .Out_5(n8_bit_adder_old_1_out_5),
    .Out_4(n8_bit_adder_old_1_out_4), .Out_3(n8_bit_adder_old_1_out_3), .Out_2(n8_bit_adder_old_1_out_2),
    .Out_1(n8_bit_adder_old_1_out_1), .Out_0(n8_bit_adder_old_1_out_0));
  LED led_1 (.in(n8_bit_adder_old_1_out_7));
  LED led_2 (.in(n8_bit_adder_old_1_out_6));
  LED led_3 (.in(n8_bit_adder_old_1_out_4));
  LED led_4 (.in(n8_bit_adder_old_1_out_5));
  LED led_5 (.in(n8_bit_adder_old_1_out_2));
  LED led_6 (.in(n8_bit_adder_old_1_out_3));
  LED led_7 (.in(n8_bit_adder_old_1_out_1));
  LED led_8 (.in(n8_bit_adder_old_1_out_0));
endmodule

module _8_Bit_Adder (
  input  B_7,
  input  B_6,
  input  B_5,
  input  B_4,
  input  B_3,
  input  B_2,
  input  B_1,
  input  B_0,
  input  A_7,
  input  A_6,
  input  A_5,
  input  A_4,
  input  A_3,
  input  A_2,
  input  A_1,
  input  A_0,
  input  Carry_In,
  output Carry_Out,
  output Out_7,
  output Out_6,
  output Out_5,
  output Out_4,
  output Out_3,
  output Out_2,
  output Out_1,
  output Out_0
);

  wire adder_1_c_out, adder_2_c_out, adder_3_c_out, adder_4_c_out, adder_5_c_out, adder_6_c_out,
       adder_7_c_out;

  adder adder_1 (._1(B_0), ._2(A_0), .C_in(Carry_In), .A_out(Out_0), .C_out(adder_1_c_out));
  adder adder_2 (._1(B_2), ._2(A_2), .C_in(adder_3_c_out), .A_out(Out_2), .C_out(adder_2_c_out));
  adder adder_3 (._1(B_1), ._2(A_1), .C_in(adder_1_c_out), .A_out(Out_1), .C_out(adder_3_c_out));
  adder adder_4 (._1(B_4), ._2(A_4), .C_in(adder_5_c_out), .A_out(Out_4), .C_out(adder_4_c_out));
  adder adder_5 (._1(B_3), ._2(A_3), .C_in(adder_2_c_out), .A_out(Out_3), .C_out(adder_5_c_out));
  adder adder_6 (._1(B_6), ._2(A_6), .C_in(adder_7_c_out), .A_out(Out_6), .C_out(adder_6_c_out));
  adder adder_7 (._1(B_5), ._2(A_5), .C_in(adder_4_c_out), .A_out(Out_5), .C_out(adder_7_c_out));
  adder adder_8 (._1(B_7), ._2(A_7), .C_in(adder_6_c_out), .A_out(Out_7), .C_out(Carry_Out));
endmodule

module _8_Bit_Twos_Compliment (
  input  A_7,
  input  A_6,
  input  A_5,
  input  A_4,
  input  A_3,
  input  A_2,
  input  A_1,
  input  A_0,
  output Out_7,
  output Out_6,
  output Out_5,
  output Out_4,
  output Out_3,
  output Out_2,
  output Out_1,
  output Out_0
);

  wire not_1_out, not_2_out, not_3_out, not_4_out, not_5_out, not_6_out, not_7_out, not_8_out;

  not not_1 (not_1_out, A_7);
  not not_2 (not_2_out, A_6);
  not not_3 (not_3_out, A_5);
  not not_4 (not_4_out, A_4);
  not not_5 (not_5_out, A_3);
  not not_6 (not_6_out, A_2);
  not not_7 (not_7_out, A_1);
  not not_8 (not_8_out, A_0);
  _8_Bit_Adder u_8_bit_adder_1 (
    .B_7(1'b0), .B_6(1'b0), .B_5(1'b0), .B_4(1'b0), .B_3(1'b0), .B_2(1'b0), .B_1(1'b0), .B_0(1'b1),
    .A_7(not_1_out), .A_6(not_2_out), .A_5(not_3_out), .A_4(not_4_out), .A_3(not_5_out), .A_2(not_6_out),
    .A_1(not_7_out), .A_0(not_8_out), .Carry_Out(Out_7), .Out_7(Out_6), .Out_6(Out_5), .Out_5(Out_4),
    .Out_4(Out_3), .Out_3(Out_2), .Out_2(Out_1), .Out_1(Out_0));  // open: Carry_In, Out_0

  // Notes on the sheet:
  //   Two's Compliment, (Flip and Add One)
endmodule

module _8_Bit_ALU (
  input  in_1,
  input  in_2
);

  wire nand_1_out;

  nand nand_1 (nand_1_out, in_1, in_2);
endmodule

module _1_Bit_Selector (
  input  B,
  input  A,
  input  Selector,
  output Out
);

  wire and_1_out, and_2_out, not_1_out, not_2_out;

  not not_1 (not_1_out, not_2_out);
  not not_2 (not_2_out, Selector);
  and and_1 (and_1_out, B, not_1_out);
  or or_1 (Out, and_1_out, and_2_out);
  and and_2 (and_2_out, A, not_2_out);
endmodule

module _8_Bit_Selector (
  input  B_7,
  input  B_6,
  input  B_5,
  input  B_4,
  input  B_3,
  input  B_2,
  input  B_1,
  input  B_0,
  input  A_7,
  input  A_6,
  input  A_5,
  input  A_4,
  input  A_3,
  input  A_2,
  input  Selector,
  input  A_1,
  input  A_0,
  output Out_7,
  output Out_6,
  output Out_5,
  output Out_4,
  output Out_3,
  output Out_2,
  output Out_1,
  output Out_0
);

  _1_Bit_Selector u_1_bit_selector_1 (.B(B_7), .A(A_7), .Selector(Selector), .Out(Out_7));
  _1_Bit_Selector u_1_bit_selector_2 (.B(B_6), .A(A_6), .Selector(Selector), .Out(Out_6));
  _1_Bit_Selector u_1_bit_selector_3 (.B(B_5), .A(A_5), .Selector(Selector), .Out(Out_5));
  _1_Bit_Selector u_1_bit_selector_4 (.B(B_4), .A(A_4), .Selector(Selector), .Out(Out_4));
  _1_Bit_Selector u_1_bit_selector_5 (.B(B_3), .A(A_3), .Selector(Selector), .Out(Out_3));
  _1_Bit_Selector u_1_bit_selector_6 (.B(B_2), .A(A_2), .Selector(Selector), .Out(Out_2));
  _1_Bit_Selector u_1_bit_selector_7 (.B(B_1), .A(A_1), .Selector(Selector), .Out(Out_1));
  _1_Bit_Selector u_1_bit_selector_8 (.B(B_0), .A(A_0), .Selector(Selector), .Out(Out_0));
endmodule

module _1_Bit_Register (
  input  Reset,
  input  A,
  input  Set,
  output Out
);

  wire and_1_out, and_2_out, nor_1_out, nor_2_out, not_1_out, or_1_out;

  not not_1 (not_1_out, Reset);
  and and_1 (and_1_out, not_1_out, A);
  or or_1 (or_1_out, Reset, Set);
  and and_2 (and_2_out, and_1_out, or_1_out);
  nor nor_1 (nor_1_out, and_2_out, nor_2_out);
  nor nor_2 (nor_2_out, nor_1_out, or_1_out);
  not not_2 (Out, nor_1_out);
endmodule

// Register
module _8_Bit_Register (
  input  Reset,
  input  In_7,
  input  In_6,
  input  In_5,
  input  In_4,
  input  In_3,
  input  In_2,
  input  In_1,
  input  In_0,
  input  Set,
  output Out_7,
  output Out_6,
  output Out_5,
  output Out_4,
  output Out_3,
  output Out_2,
  output Out_1,
  output Out_0
);

  _1_Bit_Register u_1_bit_register_1 (.A(In_7), .Reset(Reset), .Set(Set), .Out(Out_7));
  _1_Bit_Register u_1_bit_register_2 (.A(In_6), .Reset(Reset), .Set(Set), .Out(Out_6));
  _1_Bit_Register u_1_bit_register_3 (.A(In_5), .Reset(Reset), .Set(Set), .Out(Out_5));
  _1_Bit_Register u_1_bit_register_4 (.A(In_4), .Reset(Reset), .Set(Set), .Out(Out_4));
  _1_Bit_Register u_1_bit_register_5 (.A(In_3), .Reset(Reset), .Set(Set), .Out(Out_3));
  _1_Bit_Register u_1_bit_register_6 (.A(In_2), .Reset(Reset), .Set(Set), .Out(Out_2));
  _1_Bit_Register u_1_bit_register_7 (.A(In_1), .Reset(Reset), .Set(Set), .Out(Out_1));
  _1_Bit_Register u_1_bit_register_8 (.A(In_0), .Reset(Reset), .Set(Set), .Out(Out_0));
endmodule

// 4 byte
module _8_bit_RAM__4_word (
  input  Select_1,
  input  Reset,
  input  Select_0,
  input  In_7,
  input  In_6,
  input  In_5,
  input  In_4,
  input  In_3,
  input  In_2,
  input  In_1,
  input  In_0,
  input  Control_Set,
  input  Control_Get,
  output Out_7,
  output Out_6,
  output Out_5,
  output Out_4,
  output Out_3,
  output Out_2,
  output Out_1,
  output Out_0
);

  wire buffer_1_out, buffer_2_out, buffer_3_out, buffer_4_out, buffer_5_out, buffer_6_out, buffer_7_out,
       buffer_8_out, Get_Select_out_0, Get_Select_out_1, Get_Select_out_2, Get_Select_out_3,
       n8_bit_control_1_out_0, n8_bit_control_1_out_1, n8_bit_control_1_out_2, n8_bit_control_1_out_3,
       n8_bit_control_1_out_4, n8_bit_control_1_out_5, n8_bit_control_1_out_6, n8_bit_control_1_out_7,
       n8_bit_control_2_out_0, n8_bit_control_2_out_1, n8_bit_control_2_out_2, n8_bit_control_2_out_3,
       n8_bit_control_2_out_4, n8_bit_control_2_out_5, n8_bit_control_2_out_6, n8_bit_control_2_out_7,
       n8_bit_control_3_out_0, n8_bit_control_3_out_1, n8_bit_control_3_out_2, n8_bit_control_3_out_3,
       n8_bit_control_3_out_4, n8_bit_control_3_out_5, n8_bit_control_3_out_6, n8_bit_control_3_out_7,
       n8_bit_control_4_out_0, n8_bit_control_4_out_1, n8_bit_control_4_out_2, n8_bit_control_4_out_3,
       n8_bit_control_4_out_4, n8_bit_control_4_out_5, n8_bit_control_4_out_6, n8_bit_control_4_out_7,
       n8_bit_control_5_out_0, n8_bit_control_5_out_1, n8_bit_control_5_out_2, n8_bit_control_5_out_3,
       n8_bit_control_5_out_4, n8_bit_control_5_out_5, n8_bit_control_5_out_6, n8_bit_control_5_out_7,
       n8_bit_control_6_out_0, n8_bit_control_6_out_1, n8_bit_control_6_out_2, n8_bit_control_6_out_3,
       n8_bit_control_6_out_4, n8_bit_control_6_out_5, n8_bit_control_6_out_6, n8_bit_control_6_out_7,
       n8_bit_control_7_out_0, n8_bit_control_7_out_1, n8_bit_control_7_out_2, n8_bit_control_7_out_3,
       n8_bit_control_7_out_4, n8_bit_control_7_out_5, n8_bit_control_7_out_6, n8_bit_control_7_out_7,
       n8_bit_control_8_out_0, n8_bit_control_8_out_1, n8_bit_control_8_out_2, n8_bit_control_8_out_3,
       n8_bit_control_8_out_4, n8_bit_control_8_out_5, n8_bit_control_8_out_6, n8_bit_control_8_out_7,
       n8_bit_register_1_out_0, n8_bit_register_1_out_1, n8_bit_register_1_out_2, n8_bit_register_1_out_3,
       n8_bit_register_1_out_4, n8_bit_register_1_out_5, n8_bit_register_1_out_6, n8_bit_register_1_out_7,
       n8_bit_register_2_out_0, n8_bit_register_2_out_1, n8_bit_register_2_out_2, n8_bit_register_2_out_3,
       n8_bit_register_2_out_4, n8_bit_register_2_out_5, n8_bit_register_2_out_6, n8_bit_register_2_out_7,
       n8_bit_register_3_out_0, n8_bit_register_3_out_1, n8_bit_register_3_out_2, n8_bit_register_3_out_3,
       n8_bit_register_3_out_4, n8_bit_register_3_out_5, n8_bit_register_3_out_6, n8_bit_register_3_out_7,
       n8_bit_register_4_out_0, n8_bit_register_4_out_1, n8_bit_register_4_out_2, n8_bit_register_4_out_3,
       n8_bit_register_4_out_4, n8_bit_register_4_out_5, n8_bit_register_4_out_6, n8_bit_register_4_out_7,
       Set_Select_out_0, Set_Select_out_1, Set_Select_out_2, Set_Select_out_3;

  buf buffer_1 (buffer_1_out, In_6);
  buf buffer_2 (buffer_2_out, In_5);
  buf buffer_3 (buffer_3_out, In_7);
  buf buffer_4 (buffer_4_out, In_3);
  buf buffer_5 (buffer_5_out, In_2);
  buf buffer_6 (buffer_6_out, In_4);
  buf buffer_7 (buffer_7_out, In_1);
  buf buffer_8 (buffer_8_out, In_0);
  _2_Bit_Decode Get_Select (
    .In_1(Select_1), .In_0(Select_0), .Decode(Control_Get), .Out_3(Get_Select_out_3),
    .Out_2(Get_Select_out_2), .Out_1(Get_Select_out_1), .Out_0(Get_Select_out_0));
  _2_Bit_Decode Set_Select (
    .In_1(Select_1), .In_0(Select_0), .Decode(Control_Set), .Out_3(Set_Select_out_3),
    .Out_2(Set_Select_out_2), .Out_1(Set_Select_out_1), .Out_0(Set_Select_out_0));
  _8_Bit_Register u_8_bit_register_1 (
    .In_7(buffer_3_out), .In_6(buffer_1_out), .In_5(buffer_2_out), .In_4(buffer_6_out), .In_3(buffer_4_out),
    .In_2(buffer_5_out), .In_1(buffer_7_out), .In_0(buffer_8_out), .Reset(Reset), .Set(Set_Select_out_3),
    .Out_7(n8_bit_register_1_out_7), .Out_6(n8_bit_register_1_out_6), .Out_5(n8_bit_register_1_out_5),
    .Out_4(n8_bit_register_1_out_4), .Out_3(n8_bit_register_1_out_3), .Out_2(n8_bit_register_1_out_2),
    .Out_1(n8_bit_register_1_out_1), .Out_0(n8_bit_register_1_out_0));
  _8_Bit_Register u_8_bit_register_2 (
    .In_7(buffer_3_out), .In_6(buffer_1_out), .In_5(buffer_2_out), .In_4(buffer_6_out), .In_3(buffer_4_out),
    .In_2(buffer_5_out), .In_1(buffer_7_out), .In_0(buffer_8_out), .Reset(Reset), .Set(Set_Select_out_2),
    .Out_7(n8_bit_register_2_out_7), .Out_6(n8_bit_register_2_out_6), .Out_5(n8_bit_register_2_out_5),
    .Out_4(n8_bit_register_2_out_4), .Out_3(n8_bit_register_2_out_3), .Out_2(n8_bit_register_2_out_2),
    .Out_1(n8_bit_register_2_out_1), .Out_0(n8_bit_register_2_out_0));
  _8_Bit_Register u_8_bit_register_3 (
    .In_7(buffer_3_out), .In_6(buffer_1_out), .In_5(buffer_2_out), .In_4(buffer_6_out), .In_3(buffer_4_out),
    .In_2(buffer_5_out), .In_1(buffer_7_out), .In_0(buffer_8_out), .Reset(Reset), .Set(Set_Select_out_1),
    .Out_7(n8_bit_register_3_out_7), .Out_6(n8_bit_register_3_out_6), .Out_5(n8_bit_register_3_out_5),
    .Out_4(n8_bit_register_3_out_4), .Out_3(n8_bit_register_3_out_3), .Out_2(n8_bit_register_3_out_2),
    .Out_1(n8_bit_register_3_out_1), .Out_0(n8_bit_register_3_out_0));
  _8_Bit_Register u_8_bit_register_4 (
    .In_7(buffer_3_out), .In_6(buffer_1_out), .In_5(buffer_2_out), .In_4(buffer_6_out), .In_3(buffer_4_out),
    .In_2(buffer_5_out), .In_1(buffer_7_out), .In_0(buffer_8_out), .Reset(Reset), .Set(Set_Select_out_0),
    .Out_7(n8_bit_register_4_out_7), .Out_6(n8_bit_register_4_out_6), .Out_5(n8_bit_register_4_out_5),
    .Out_4(n8_bit_register_4_out_4), .Out_3(n8_bit_register_4_out_3), .Out_2(n8_bit_register_4_out_2),
    .Out_1(n8_bit_register_4_out_1), .Out_0(n8_bit_register_4_out_0));
  _8_Bit_Control u_8_bit_control_1 (
    .In_7(n8_bit_control_2_out_7), .In_6(n8_bit_control_2_out_6), .In_5(n8_bit_control_2_out_5),
    .In_4(n8_bit_control_2_out_4), .In_3(n8_bit_control_2_out_3), .In_2(n8_bit_control_2_out_2),
    .In_1(n8_bit_control_2_out_1), .In_0(n8_bit_control_2_out_0), .Let(Control_Get),
    .Out_7(n8_bit_control_1_out_7), .Out_6(n8_bit_control_1_out_6), .Out_5(n8_bit_control_1_out_5),
    .Out_4(n8_bit_control_1_out_4), .Out_3(n8_bit_control_1_out_3), .Out_2(n8_bit_control_1_out_2),
    .Out_1(n8_bit_control_1_out_1), .Out_0(n8_bit_control_1_out_0));
  _8_Bit_Control u_8_bit_control_2 (
    .In_7(n8_bit_register_1_out_7), .In_6(n8_bit_register_1_out_6), .In_5(n8_bit_register_1_out_5),
    .In_4(n8_bit_register_1_out_4), .In_3(n8_bit_register_1_out_3), .In_2(n8_bit_register_1_out_2),
    .In_1(n8_bit_register_1_out_1), .In_0(n8_bit_register_1_out_0), .Let(Get_Select_out_3),
    .Out_7(n8_bit_control_2_out_7), .Out_6(n8_bit_control_2_out_6), .Out_5(n8_bit_control_2_out_5),
    .Out_4(n8_bit_control_2_out_4), .Out_3(n8_bit_control_2_out_3), .Out_2(n8_bit_control_2_out_2),
    .Out_1(n8_bit_control_2_out_1), .Out_0(n8_bit_control_2_out_0));
  _8_Bit_Control u_8_bit_control_3 (
    .In_7(n8_bit_control_4_out_7), .In_6(n8_bit_control_4_out_6), .In_5(n8_bit_control_4_out_5),
    .In_4(n8_bit_control_4_out_4), .In_3(n8_bit_control_4_out_3), .In_2(n8_bit_control_4_out_2),
    .In_1(n8_bit_control_4_out_1), .In_0(n8_bit_control_4_out_0), .Let(Control_Get),
    .Out_7(n8_bit_control_3_out_7), .Out_6(n8_bit_control_3_out_6), .Out_5(n8_bit_control_3_out_5),
    .Out_4(n8_bit_control_3_out_4), .Out_3(n8_bit_control_3_out_3), .Out_2(n8_bit_control_3_out_2),
    .Out_1(n8_bit_control_3_out_1), .Out_0(n8_bit_control_3_out_0));
  _8_Bit_Control u_8_bit_control_4 (
    .In_7(n8_bit_register_2_out_7), .In_6(n8_bit_register_2_out_6), .In_5(n8_bit_register_2_out_5),
    .In_4(n8_bit_register_2_out_4), .In_3(n8_bit_register_2_out_3), .In_2(n8_bit_register_2_out_2),
    .In_1(n8_bit_register_2_out_1), .In_0(n8_bit_register_2_out_0), .Let(Get_Select_out_2),
    .Out_7(n8_bit_control_4_out_7), .Out_6(n8_bit_control_4_out_6), .Out_5(n8_bit_control_4_out_5),
    .Out_4(n8_bit_control_4_out_4), .Out_3(n8_bit_control_4_out_3), .Out_2(n8_bit_control_4_out_2),
    .Out_1(n8_bit_control_4_out_1), .Out_0(n8_bit_control_4_out_0));
  _8_Bit_Control u_8_bit_control_5 (
    .In_7(n8_bit_control_6_out_7), .In_6(n8_bit_control_6_out_6), .In_5(n8_bit_control_6_out_5),
    .In_4(n8_bit_control_6_out_4), .In_3(n8_bit_control_6_out_3), .In_2(n8_bit_control_6_out_2),
    .In_1(n8_bit_control_6_out_1), .In_0(n8_bit_control_6_out_0), .Let(Control_Get),
    .Out_7(n8_bit_control_5_out_7), .Out_6(n8_bit_control_5_out_6), .Out_5(n8_bit_control_5_out_5),
    .Out_4(n8_bit_control_5_out_4), .Out_3(n8_bit_control_5_out_3), .Out_2(n8_bit_control_5_out_2),
    .Out_1(n8_bit_control_5_out_1), .Out_0(n8_bit_control_5_out_0));
  _8_Bit_Control u_8_bit_control_6 (
    .In_7(n8_bit_register_3_out_7), .In_6(n8_bit_register_3_out_6), .In_5(n8_bit_register_3_out_5),
    .In_4(n8_bit_register_3_out_4), .In_3(n8_bit_register_3_out_3), .In_2(n8_bit_register_3_out_2),
    .In_1(n8_bit_register_3_out_1), .In_0(n8_bit_register_3_out_0), .Let(Get_Select_out_1),
    .Out_7(n8_bit_control_6_out_7), .Out_6(n8_bit_control_6_out_6), .Out_5(n8_bit_control_6_out_5),
    .Out_4(n8_bit_control_6_out_4), .Out_3(n8_bit_control_6_out_3), .Out_2(n8_bit_control_6_out_2),
    .Out_1(n8_bit_control_6_out_1), .Out_0(n8_bit_control_6_out_0));
  _8_Bit_Control u_8_bit_control_7 (
    .In_7(n8_bit_register_4_out_7), .In_6(n8_bit_register_4_out_6), .In_5(n8_bit_register_4_out_5),
    .In_4(n8_bit_register_4_out_4), .In_3(n8_bit_register_4_out_3), .In_2(n8_bit_register_4_out_2),
    .In_1(n8_bit_register_4_out_1), .In_0(n8_bit_register_4_out_0), .Let(Get_Select_out_0),
    .Out_7(n8_bit_control_7_out_7), .Out_6(n8_bit_control_7_out_6), .Out_5(n8_bit_control_7_out_5),
    .Out_4(n8_bit_control_7_out_4), .Out_3(n8_bit_control_7_out_3), .Out_2(n8_bit_control_7_out_2),
    .Out_1(n8_bit_control_7_out_1), .Out_0(n8_bit_control_7_out_0));
  _8_Bit_Control u_8_bit_control_8 (
    .In_7(n8_bit_control_7_out_7), .In_6(n8_bit_control_7_out_6), .In_5(n8_bit_control_7_out_5),
    .In_4(n8_bit_control_7_out_4), .In_3(n8_bit_control_7_out_3), .In_2(n8_bit_control_7_out_2),
    .In_1(n8_bit_control_7_out_1), .In_0(n8_bit_control_7_out_0), .Let(Control_Get),
    .Out_7(n8_bit_control_8_out_7), .Out_6(n8_bit_control_8_out_6), .Out_5(n8_bit_control_8_out_5),
    .Out_4(n8_bit_control_8_out_4), .Out_3(n8_bit_control_8_out_3), .Out_2(n8_bit_control_8_out_2),
    .Out_1(n8_bit_control_8_out_1), .Out_0(n8_bit_control_8_out_0));
  _4_Bit_Or u_4_bit_or_1 (
    .in_1(n8_bit_control_1_out_0), .in_2(n8_bit_control_3_out_0), .in_3(n8_bit_control_5_out_0),
    .in_4(n8_bit_control_8_out_0), .out_5(Out_0));
  _4_Bit_Or u_4_bit_or_2 (
    .in_1(n8_bit_control_1_out_2), .in_2(n8_bit_control_3_out_2), .in_3(n8_bit_control_5_out_2),
    .in_4(n8_bit_control_8_out_2), .out_5(Out_2));
  _4_Bit_Or u_4_bit_or_3 (
    .in_1(n8_bit_control_1_out_1), .in_2(n8_bit_control_3_out_1), .in_3(n8_bit_control_5_out_1),
    .in_4(n8_bit_control_8_out_1), .out_5(Out_1));
  _4_Bit_Or u_4_bit_or_4 (
    .in_1(n8_bit_control_1_out_4), .in_2(n8_bit_control_3_out_4), .in_3(n8_bit_control_5_out_4),
    .in_4(n8_bit_control_8_out_4), .out_5(Out_4));
  _4_Bit_Or u_4_bit_or_5 (
    .in_1(n8_bit_control_1_out_3), .in_2(n8_bit_control_3_out_3), .in_3(n8_bit_control_5_out_3),
    .in_4(n8_bit_control_8_out_3), .out_5(Out_3));
  _4_Bit_Or u_4_bit_or_6 (
    .in_1(n8_bit_control_1_out_5), .in_2(n8_bit_control_3_out_5), .in_3(n8_bit_control_5_out_5),
    .in_4(n8_bit_control_8_out_5), .out_5(Out_5));
  _4_Bit_Or u_4_bit_or_7 (
    .in_1(n8_bit_control_1_out_6), .in_2(n8_bit_control_3_out_6), .in_3(n8_bit_control_5_out_6),
    .in_4(n8_bit_control_8_out_6), .out_5(Out_6));
  _4_Bit_Or u_4_bit_or_8 (
    .in_1(n8_bit_control_1_out_7), .in_2(n8_bit_control_3_out_7), .in_3(n8_bit_control_5_out_7),
    .in_4(n8_bit_control_8_out_7), .out_5(Out_7));
endmodule

module _2_Bit_Decode (
  input  In_1,
  input  In_0,
  input  Decode,
  output Out_3,
  output Out_2,
  output Out_1,
  output Out_0
);

  wire and_1_out, and_2_out, and_3_out, and_4_out, not_1_out, not_2_out, not_3_out, not_4_out;

  not not_1 (not_1_out, In_1);
  not not_2 (not_2_out, In_0);
  not not_3 (not_3_out, not_1_out);
  not not_4 (not_4_out, not_2_out);
  and and_1 (and_1_out, not_4_out, not_3_out);
  and and_2 (and_2_out, not_2_out, not_3_out);
  and and_3 (and_3_out, not_1_out, not_4_out);
  and and_4 (and_4_out, not_2_out, not_1_out);
  and and_5 (Out_3, and_1_out, Decode);
  and and_6 (Out_2, and_2_out, Decode);
  and and_7 (Out_1, and_3_out, Decode);
  and and_8 (Out_0, and_4_out, Decode);
endmodule

module _4_Bit_Decode (
  input  In_3,
  input  In_2,
  input  In_1,
  input  In_0,
  input  Decode,
  output out_6,
  output out_7,
  output out_8,
  output out_9,
  output out_10,
  output out_11,
  output out_12,
  output out_13,
  output out_14,
  output out_15,
  output out_16,
  output out_17,
  output out_18,
  output out_19,
  output out_20,
  output out_21
);

  wire and_1_out, and_2_out, and_3_out, and_4_out, n2_bit_decode_1_out_0, n2_bit_decode_1_out_1,
       n2_bit_decode_1_out_2, n2_bit_decode_1_out_3, n2_bit_decode_2_out_0, n2_bit_decode_2_out_1,
       n2_bit_decode_2_out_2, n2_bit_decode_2_out_3, n2_bit_decode_3_out_0, n2_bit_decode_3_out_1,
       n2_bit_decode_3_out_2, n2_bit_decode_3_out_3, n2_bit_decode_4_out_0, n2_bit_decode_4_out_1,
       n2_bit_decode_4_out_2, n2_bit_decode_4_out_3, not_1_out, not_2_out;

  not not_1 (not_1_out, In_3);
  not not_2 (not_2_out, In_2);
  _2_Bit_Decode u_2_bit_decode_1 (
    .In_1(In_1), .In_0(In_0), .Decode(and_1_out), .Out_3(n2_bit_decode_1_out_3),
    .Out_2(n2_bit_decode_1_out_2), .Out_1(n2_bit_decode_1_out_1), .Out_0(n2_bit_decode_1_out_0));
  and and_1 (and_1_out, not_1_out, not_2_out);
  and and_2 (and_2_out, not_1_out, In_2);
  and and_3 (and_3_out, In_3, not_2_out);
  and and_4 (and_4_out, In_3, In_2);
  _2_Bit_Decode u_2_bit_decode_2 (
    .In_1(In_1), .In_0(In_0), .Decode(and_3_out), .Out_3(n2_bit_decode_2_out_3),
    .Out_2(n2_bit_decode_2_out_2), .Out_1(n2_bit_decode_2_out_1), .Out_0(n2_bit_decode_2_out_0));
  _2_Bit_Decode u_2_bit_decode_3 (
    .In_1(In_1), .In_0(In_0), .Decode(and_2_out), .Out_3(n2_bit_decode_3_out_3),
    .Out_2(n2_bit_decode_3_out_2), .Out_1(n2_bit_decode_3_out_1), .Out_0(n2_bit_decode_3_out_0));
  _2_Bit_Decode u_2_bit_decode_4 (
    .In_1(In_1), .In_0(In_0), .Decode(and_4_out), .Out_3(n2_bit_decode_4_out_3),
    .Out_2(n2_bit_decode_4_out_2), .Out_1(n2_bit_decode_4_out_1), .Out_0(n2_bit_decode_4_out_0));
  and and_5 (out_14, Decode, n2_bit_decode_3_out_3);
  and and_6 (out_15, Decode, n2_bit_decode_3_out_2);
  and and_7 (out_16, Decode, n2_bit_decode_3_out_1);
  and and_8 (out_17, Decode, n2_bit_decode_3_out_0);
  and and_9 (out_18, Decode, n2_bit_decode_1_out_3);
  and and_10 (out_19, Decode, n2_bit_decode_1_out_2);
  and and_11 (out_20, Decode, n2_bit_decode_1_out_1);
  and and_12 (out_21, Decode, n2_bit_decode_1_out_0);
  and and_13 (out_6, Decode, n2_bit_decode_4_out_3);
  and and_14 (out_7, Decode, n2_bit_decode_4_out_2);
  and and_15 (out_8, Decode, n2_bit_decode_4_out_1);
  and and_16 (out_9, Decode, n2_bit_decode_4_out_0);
  and and_17 (out_10, Decode, n2_bit_decode_2_out_3);
  and and_18 (out_11, Decode, n2_bit_decode_2_out_2);
  and and_19 (out_12, Decode, n2_bit_decode_2_out_1);
  and and_20 (out_13, Decode, n2_bit_decode_2_out_0);
endmodule

// Control
module _8_Bit_Control (
  input  In_7,
  input  In_6,
  input  In_5,
  input  In_4,
  input  In_3,
  input  In_2,
  input  In_1,
  input  In_0,
  input  Let,
  output Out_7,
  output Out_6,
  output Out_5,
  output Out_4,
  output Out_3,
  output Out_2,
  output Out_1,
  output Out_0
);

  and and_1 (Out_7, In_7, Let);
  and and_2 (Out_6, In_6, Let);
  and and_3 (Out_5, In_5, Let);
  and and_4 (Out_4, In_4, Let);
  and and_5 (Out_3, In_3, Let);
  and and_6 (Out_2, In_2, Let);
  and and_7 (Out_1, In_1, Let);
  and and_8 (Out_0, In_0, Let);
endmodule

// OR
module _4_Bit_Or (
  input  in_1,
  input  in_2,
  input  in_3,
  input  in_4,
  output out_5
);

  wire or_1_out, or_2_out;

  or or_1 (or_1_out, in_1, in_2);
  or or_2 (or_2_out, in_3, in_4);
  or or_3 (out_5, or_1_out, or_2_out);
endmodule

module RAM_Adapter (
  input  in_1,
  input  in_2,
  input  in_3,
  input  in_4,
  output out_5,
  output out_6,
  output out_7,
  output out_8,
  output out_9,
  output out_10,
  output out_11,
  output out_12
);

  wire n2_bit_decode_1_out_0, n2_bit_decode_1_out_1, n2_bit_decode_1_out_2, n2_bit_decode_1_out_3;

  _2_Bit_Decode u_2_bit_decode_1 (
    .In_1(in_1), .In_0(in_2), .Decode(1'b1), .Out_3(n2_bit_decode_1_out_3), .Out_2(n2_bit_decode_1_out_2),
    .Out_1(n2_bit_decode_1_out_1), .Out_0(n2_bit_decode_1_out_0));
  and and_1 (out_5, n2_bit_decode_1_out_3, in_3);
  and and_2 (out_6, n2_bit_decode_1_out_3, in_4);
  and and_3 (out_7, n2_bit_decode_1_out_2, in_3);
  and and_4 (out_8, n2_bit_decode_1_out_2, in_4);
  and and_5 (out_9, n2_bit_decode_1_out_1, in_3);
  and and_6 (out_10, n2_bit_decode_1_out_1, in_4);
  and and_7 (out_11, n2_bit_decode_1_out_0, in_3);
  and and_8 (out_12, n2_bit_decode_1_out_0, in_4);
endmodule

// RAM 16
module _8_bit_RAM__16_word (
  input  Select_3,
  input  Reset,
  input  Select_2,
  input  Select_1,
  input  Select_0,
  input  In_7,
  input  In_6,
  input  In_5,
  input  In_4,
  input  In_3,
  input  In_2,
  input  In_1,
  input  In_0,
  input  Set,
  input  Get,
  output Out_7,
  output Out_6,
  output Out_5,
  output Out_4,
  output Out_3,
  output Out_2,
  output Out_1,
  output Out_0
);

  wire Address_Adapter_out_5, Address_Adapter_out_6, Address_Adapter_out_7, Address_Adapter_out_8,
       Address_Adapter_out_9, Address_Adapter_out_10, Address_Adapter_out_11, Address_Adapter_out_12,
       and_1_out, and_2_out, and_3_out, and_4_out, and_5_out, and_6_out, and_7_out, and_8_out,
       n2_bit_decode_1_out_0, n2_bit_decode_1_out_1, n2_bit_decode_1_out_2, n2_bit_decode_1_out_3,
       n8_bit_ram_4_word_1_out_0, n8_bit_ram_4_word_1_out_1, n8_bit_ram_4_word_1_out_2,
       n8_bit_ram_4_word_1_out_3, n8_bit_ram_4_word_1_out_4, n8_bit_ram_4_word_1_out_5,
       n8_bit_ram_4_word_1_out_6, n8_bit_ram_4_word_1_out_7, n8_bit_ram_4_word_2_out_0,
       n8_bit_ram_4_word_2_out_1, n8_bit_ram_4_word_2_out_2, n8_bit_ram_4_word_2_out_3,
       n8_bit_ram_4_word_2_out_4, n8_bit_ram_4_word_2_out_5, n8_bit_ram_4_word_2_out_6,
       n8_bit_ram_4_word_2_out_7, n8_bit_ram_4_word_3_out_0, n8_bit_ram_4_word_3_out_1,
       n8_bit_ram_4_word_3_out_2, n8_bit_ram_4_word_3_out_3, n8_bit_ram_4_word_3_out_4,
       n8_bit_ram_4_word_3_out_5, n8_bit_ram_4_word_3_out_6, n8_bit_ram_4_word_3_out_7,
       n8_bit_ram_4_word_4_out_0, n8_bit_ram_4_word_4_out_1, n8_bit_ram_4_word_4_out_2,
       n8_bit_ram_4_word_4_out_3, n8_bit_ram_4_word_4_out_4, n8_bit_ram_4_word_4_out_5,
       n8_bit_ram_4_word_4_out_6, n8_bit_ram_4_word_4_out_7;

  RAM_Adapter Address_Adapter (
    .in_1(Select_3), .in_2(Select_2), .in_3(Select_1), .in_4(Select_0), .out_5(Address_Adapter_out_5),
    .out_6(Address_Adapter_out_6), .out_7(Address_Adapter_out_7), .out_8(Address_Adapter_out_8),
    .out_9(Address_Adapter_out_9), .out_10(Address_Adapter_out_10), .out_11(Address_Adapter_out_11),
    .out_12(Address_Adapter_out_12));
  _2_Bit_Decode u_2_bit_decode_1 (
    .In_1(Select_3), .In_0(Select_2), .Decode(1'b1), .Out_3(n2_bit_decode_1_out_3),
    .Out_2(n2_bit_decode_1_out_2), .Out_1(n2_bit_decode_1_out_1), .Out_0(n2_bit_decode_1_out_0));
  and and_1 (and_1_out, Set, n2_bit_decode_1_out_3);
  and and_2 (and_2_out, Set, n2_bit_decode_1_out_2);
  and and_3 (and_3_out, Set, n2_bit_decode_1_out_1);
  and and_4 (and_4_out, Set, n2_bit_decode_1_out_0);
  _8_bit_RAM__4_word u_8_bit_ram_4_word_1 (
    .Select_1(Address_Adapter_out_11), .Select_0(Address_Adapter_out_12), .In_7(In_7), .In_6(In_6),
    .In_5(In_5), .In_4(In_4), .In_3(In_3), .In_2(In_2), .In_1(In_1), .In_0(In_0), .Reset(Reset),
    .Control_Set(and_4_out), .Control_Get(and_8_out), .Out_7(n8_bit_ram_4_word_1_out_7),
    .Out_6(n8_bit_ram_4_word_1_out_6), .Out_5(n8_bit_ram_4_word_1_out_5), .Out_4(n8_bit_ram_4_word_1_out_4),
    .Out_3(n8_bit_ram_4_word_1_out_3), .Out_2(n8_bit_ram_4_word_1_out_2), .Out_1(n8_bit_ram_4_word_1_out_1),
    .Out_0(n8_bit_ram_4_word_1_out_0));
  and and_5 (and_5_out, Get, n2_bit_decode_1_out_3);
  and and_6 (and_6_out, Get, n2_bit_decode_1_out_2);
  and and_7 (and_7_out, Get, n2_bit_decode_1_out_1);
  and and_8 (and_8_out, Get, n2_bit_decode_1_out_0);
  _8_bit_RAM__4_word u_8_bit_ram_4_word_2 (
    .Select_1(Address_Adapter_out_7), .Select_0(Address_Adapter_out_8), .In_7(In_7), .In_6(In_6),
    .In_5(In_5), .In_4(In_4), .In_3(In_3), .In_2(In_2), .In_1(In_1), .In_0(In_0), .Reset(Reset),
    .Control_Set(and_2_out), .Control_Get(and_6_out), .Out_7(n8_bit_ram_4_word_2_out_7),
    .Out_6(n8_bit_ram_4_word_2_out_6), .Out_5(n8_bit_ram_4_word_2_out_5), .Out_4(n8_bit_ram_4_word_2_out_4),
    .Out_3(n8_bit_ram_4_word_2_out_3), .Out_2(n8_bit_ram_4_word_2_out_2), .Out_1(n8_bit_ram_4_word_2_out_1),
    .Out_0(n8_bit_ram_4_word_2_out_0));
  _8_bit_RAM__4_word u_8_bit_ram_4_word_3 (
    .Select_1(Address_Adapter_out_9), .Select_0(Address_Adapter_out_10), .In_7(In_7), .In_6(In_6),
    .In_5(In_5), .In_4(In_4), .In_3(In_3), .In_2(In_2), .In_1(In_1), .In_0(In_0), .Reset(Reset),
    .Control_Set(and_3_out), .Control_Get(and_7_out), .Out_7(n8_bit_ram_4_word_3_out_7),
    .Out_6(n8_bit_ram_4_word_3_out_6), .Out_5(n8_bit_ram_4_word_3_out_5), .Out_4(n8_bit_ram_4_word_3_out_4),
    .Out_3(n8_bit_ram_4_word_3_out_3), .Out_2(n8_bit_ram_4_word_3_out_2), .Out_1(n8_bit_ram_4_word_3_out_1),
    .Out_0(n8_bit_ram_4_word_3_out_0));
  _8_bit_RAM__4_word u_8_bit_ram_4_word_4 (
    .Select_1(Address_Adapter_out_5), .Select_0(Address_Adapter_out_6), .In_7(In_7), .In_6(In_6),
    .In_5(In_5), .In_4(In_4), .In_3(In_3), .In_2(In_2), .In_1(In_1), .In_0(In_0), .Reset(Reset),
    .Control_Set(and_1_out), .Control_Get(and_5_out), .Out_7(n8_bit_ram_4_word_4_out_7),
    .Out_6(n8_bit_ram_4_word_4_out_6), .Out_5(n8_bit_ram_4_word_4_out_5), .Out_4(n8_bit_ram_4_word_4_out_4),
    .Out_3(n8_bit_ram_4_word_4_out_3), .Out_2(n8_bit_ram_4_word_4_out_2), .Out_1(n8_bit_ram_4_word_4_out_1),
    .Out_0(n8_bit_ram_4_word_4_out_0));
  _4_Bit_Or u_4_bit_or_1 (
    .in_1(n8_bit_ram_4_word_4_out_1), .in_2(n8_bit_ram_4_word_2_out_1), .in_3(n8_bit_ram_4_word_3_out_1),
    .in_4(n8_bit_ram_4_word_1_out_1), .out_5(Out_1));
  _4_Bit_Or u_4_bit_or_2 (
    .in_1(n8_bit_ram_4_word_4_out_0), .in_2(n8_bit_ram_4_word_2_out_0), .in_3(n8_bit_ram_4_word_3_out_0),
    .in_4(n8_bit_ram_4_word_1_out_0), .out_5(Out_0));
  _4_Bit_Or u_4_bit_or_3 (
    .in_1(n8_bit_ram_4_word_4_out_3), .in_2(n8_bit_ram_4_word_2_out_3), .in_3(n8_bit_ram_4_word_3_out_3),
    .in_4(n8_bit_ram_4_word_1_out_3), .out_5(Out_3));
  _4_Bit_Or u_4_bit_or_4 (
    .in_1(n8_bit_ram_4_word_4_out_2), .in_2(n8_bit_ram_4_word_2_out_2), .in_3(n8_bit_ram_4_word_3_out_2),
    .in_4(n8_bit_ram_4_word_1_out_2), .out_5(Out_2));
  _4_Bit_Or u_4_bit_or_5 (
    .in_1(n8_bit_ram_4_word_4_out_6), .in_2(n8_bit_ram_4_word_2_out_6), .in_3(n8_bit_ram_4_word_3_out_6),
    .in_4(n8_bit_ram_4_word_1_out_6), .out_5(Out_6));
  _4_Bit_Or u_4_bit_or_6 (
    .in_1(n8_bit_ram_4_word_4_out_5), .in_2(n8_bit_ram_4_word_2_out_5), .in_3(n8_bit_ram_4_word_3_out_5),
    .in_4(n8_bit_ram_4_word_1_out_5), .out_5(Out_5));
  _4_Bit_Or u_4_bit_or_7 (
    .in_1(n8_bit_ram_4_word_4_out_4), .in_2(n8_bit_ram_4_word_2_out_4), .in_3(n8_bit_ram_4_word_3_out_4),
    .in_4(n8_bit_ram_4_word_1_out_4), .out_5(Out_4));
  _4_Bit_Or u_4_bit_or_8 (
    .in_1(n8_bit_ram_4_word_4_out_7), .in_2(n8_bit_ram_4_word_2_out_7), .in_3(n8_bit_ram_4_word_3_out_7),
    .in_4(n8_bit_ram_4_word_1_out_7), .out_5(Out_7));

  // Notes on the sheet:
  //   Address Input
endmodule

module _8_bit_register_X (
  input  Reset,
  input  [7:0] Input,
  input  Set,
  output [7:0] Output
);

  _1_Bit_Register u_1_bit_register_1 (.A(Input[7]), .Reset(Reset), .Set(Set), .Out(Output[7]));
  _1_Bit_Register u_1_bit_register_2 (.A(Input[6]), .Reset(Reset), .Set(Set), .Out(Output[6]));
  _1_Bit_Register u_1_bit_register_3 (.A(Input[5]), .Reset(Reset), .Set(Set), .Out(Output[5]));
  _1_Bit_Register u_1_bit_register_4 (.A(Input[4]), .Reset(Reset), .Set(Set), .Out(Output[4]));
  _1_Bit_Register u_1_bit_register_5 (.A(Input[3]), .Reset(Reset), .Set(Set), .Out(Output[3]));
  _1_Bit_Register u_1_bit_register_6 (.A(Input[2]), .Reset(Reset), .Set(Set), .Out(Output[2]));
  _1_Bit_Register u_1_bit_register_7 (.A(Input[1]), .Reset(Reset), .Set(Set), .Out(Output[1]));
  _1_Bit_Register u_1_bit_register_8 (.A(Input[0]), .Reset(Reset), .Set(Set), .Out(Output[0]));
endmodule

module _8_bit_ram_4_word_x (
  input  Reset,
  input  [1:0] Address,
  input  [7:0] In,
  input  Set,
  input  Get,
  output [7:0] Out
);

  wire and_1_out, and_2_out, and_3_out, and_4_out, and_5_out, and_6_out, and_7_out, and_8_out,
       n2_bit_decode_1_out_0, n2_bit_decode_1_out_1, n2_bit_decode_1_out_2, n2_bit_decode_1_out_3;
  wire [7:0] n8_bit_control_x_1_out, n8_bit_control_x_2_out, n8_bit_control_x_3_out, n8_bit_control_x_4_out,
       n8_bit_or_x_1_out, n8_bit_or_x_3_out, n8_bit_register_x_1_output, n8_bit_register_x_2_output,
       n8_bit_register_x_3_output, n8_bit_register_x_4_output;

  and and_1 (and_1_out, Set, n2_bit_decode_1_out_3);
  and and_2 (and_2_out, Set, n2_bit_decode_1_out_2);
  and and_3 (and_3_out, Set, n2_bit_decode_1_out_1);
  and and_4 (and_4_out, Set, n2_bit_decode_1_out_0);
  _2_Bit_Decode u_2_bit_decode_1 (
    .In_1(Address[1]), .In_0(Address[0]), .Decode(1'b1), .Out_3(n2_bit_decode_1_out_3),
    .Out_2(n2_bit_decode_1_out_2), .Out_1(n2_bit_decode_1_out_1), .Out_0(n2_bit_decode_1_out_0));
  _8_bit_control_x u_8_bit_control_x_1 (
    .In(n8_bit_register_x_1_output), .Control(and_5_out), .Out(n8_bit_control_x_1_out));
  _8_bit_register_X u_8_bit_register_x_1 (
    .Input(In), .Reset(Reset), .Set(and_1_out), .Output(n8_bit_register_x_1_output));
  _8_bit_register_X u_8_bit_register_x_2 (
    .Input(In), .Reset(Reset), .Set(and_2_out), .Output(n8_bit_register_x_2_output));
  _8_bit_control_x u_8_bit_control_x_2 (
    .In(n8_bit_register_x_2_output), .Control(and_6_out), .Out(n8_bit_control_x_2_out));
  _8_bit_register_X u_8_bit_register_x_3 (
    .Input(In), .Reset(Reset), .Set(and_3_out), .Output(n8_bit_register_x_3_output));
  _8_bit_control_x u_8_bit_control_x_3 (
    .In(n8_bit_register_x_3_output), .Control(and_7_out), .Out(n8_bit_control_x_3_out));
  _8_bit_register_X u_8_bit_register_x_4 (
    .Input(In), .Reset(Reset), .Set(and_4_out), .Output(n8_bit_register_x_4_output));
  _8_bit_control_x u_8_bit_control_x_4 (
    .In(n8_bit_register_x_4_output), .Control(and_8_out), .Out(n8_bit_control_x_4_out));
  and and_5 (and_5_out, n2_bit_decode_1_out_3, Get);
  and and_6 (and_6_out, n2_bit_decode_1_out_2, Get);
  and and_7 (and_7_out, n2_bit_decode_1_out_1, Get);
  and and_8 (and_8_out, n2_bit_decode_1_out_0, Get);
  _8_bit_OR_x u_8_bit_or_x_1 (.In_B(n8_bit_control_x_1_out), .In_A(n8_bit_control_x_2_out), .Out(n8_bit_or_x_1_out));
  _8_bit_OR_x u_8_bit_or_x_2 (.In_B(n8_bit_or_x_1_out), .In_A(n8_bit_or_x_3_out), .Out(Out));
  _8_bit_OR_x u_8_bit_or_x_3 (.In_B(n8_bit_control_x_3_out), .In_A(n8_bit_control_x_4_out), .Out(n8_bit_or_x_3_out));
endmodule

module _8_bit_control_x (
  input  [7:0] In,
  input  Control,
  output [7:0] Out
);

  _8_Bit_Control u_8_bit_control_1 (
    .In_7(In[0]), .In_6(In[1]), .In_5(In[2]), .In_4(In[3]), .In_3(In[4]), .In_2(In[5]), .In_1(In[6]),
    .In_0(In[7]), .Let(Control), .Out_7(Out[0]), .Out_6(Out[1]), .Out_5(Out[2]), .Out_4(Out[3]),
    .Out_3(Out[4]), .Out_2(Out[5]), .Out_1(Out[6]), .Out_0(Out[7]));
endmodule

module _8_bit_OR_x (
  input  [7:0] In_B,
  input  [7:0] In_A,
  output [7:0] Out
);

  or or_1 (Out[7], In_B[7], In_A[7]);
  or or_2 (Out[6], In_B[6], In_A[6]);
  or or_3 (Out[5], In_B[5], In_A[5]);
  or or_4 (Out[4], In_B[4], In_A[4]);
  or or_5 (Out[3], In_B[3], In_A[3]);
  or or_6 (Out[2], In_B[2], In_A[2]);
  or or_7 (Out[1], In_B[1], In_A[1]);
  or or_8 (Out[0], In_B[0], In_A[0]);
endmodule

module _16_Bit_Adder (
  input  [15:0] in_1,
  input  [15:0] in_2,
  output [15:0] out_3
);

  wire n8_bit_adder_1_carry_out, n8_bit_adder_2_carry_out;

  _8_Bit_Adder u_8_bit_adder_1 (
    .B_7(in_1[15]), .B_6(in_1[14]), .B_5(in_1[13]), .B_4(in_1[12]), .B_3(in_1[11]), .B_2(in_1[10]),
    .B_1(in_1[9]), .B_0(in_1[8]), .A_7(in_2[15]), .A_6(in_2[14]), .A_5(in_2[13]), .A_4(in_2[12]),
    .A_3(in_2[11]), .A_2(in_2[10]), .A_1(in_2[9]), .A_0(in_2[8]), .Carry_In(n8_bit_adder_2_carry_out),
    .Carry_Out(n8_bit_adder_1_carry_out), .Out_7(out_3[15]), .Out_6(out_3[14]), .Out_5(out_3[13]),
    .Out_4(out_3[12]), .Out_3(out_3[11]), .Out_2(out_3[10]), .Out_1(out_3[9]), .Out_0(out_3[8]));
  _8_Bit_Adder u_8_bit_adder_2 (
    .B_7(in_1[7]), .B_6(in_1[6]), .B_5(in_1[5]), .B_4(in_1[4]), .B_3(in_1[3]), .B_2(in_1[2]), .B_1(in_1[1]),
    .B_0(in_1[0]), .A_7(in_2[7]), .A_6(in_2[6]), .A_5(in_2[5]), .A_4(in_2[4]), .A_3(in_2[3]), .A_2(in_2[2]),
    .A_1(in_2[1]), .A_0(in_2[0]), .Carry_In(1'b0), .Carry_Out(n8_bit_adder_2_carry_out), .Out_7(out_3[7]),
    .Out_6(out_3[6]), .Out_5(out_3[5]), .Out_4(out_3[4]), .Out_3(out_3[3]), .Out_2(out_3[2]),
    .Out_1(out_3[1]), .Out_0(out_3[0]));
endmodule

module \new  (
  input  in_1,
  input  in_2,
  output out_3
);

  wire nor_1_out;

  nor nor_1 (nor_1_out, in_1, out_3);
  nor nor_2 (out_3, nor_1_out, in_2);
endmodule
